# Fritzing sketch schematic (saved by Fritzing 0.9.3b)

parts:
  S5 = Pushbutton [package="[SMD]"]
  S6 = Pushbutton [package="[SMD]"]
  R1 = Resistor [tolerance=±5% resistance=10k package=THT]  # not connected
  R4 = Resistor [tolerance=±5% resistance=10k package=THT]
  Composant1 = GEMMA v2
  R3 = Resistor [tolerance=±5% resistance=10k package=THT]
  Composant2 = Adafruit Breadboard-Friendly NeoPixel [part_number="Adafruit #1312"]
  Composant3 = Adafruit Breadboard-Friendly NeoPixel [part_number="Adafruit #1312"]

nets:
  GND: S5.Pin_1, S5.Pin_2, S6.Pin_1, S6.Pin_2, Composant1.GND, Composant2.GND, Composant3.GND
  N1: R4.Pin_1, Composant1.B2, R3.Pin_0
  VDD: Composant1.3.3V, R3.Pin_1, Composant2.VDD, Composant3.VDD
  N2: Composant1.B1, Composant2.IN
  N3: Composant2.OUT, Composant3.IN

custom parts:
  GEMMA v2: Love FLORA but want a bite-sized version? Look no further, GEMMA is a tiny wearable platform board with a lot of might in a 1" diameter package. Powered by a Attiny85 and programmable with an Arduino IDE over USB, you'll be able to realize any wearable project! We wanted to design a microcontroller board that was small enough to fit into any project, and low cost enough to use without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
  Adafruit Breadboard-Friendly NeoPixel: This is the easiest way possible to add small, bright RGB pixels to your project. We took the same technology from our Flora NeoPixels and made them breadboard friendly, with two rows of 3 x 0.1" spaced header on each side for easy soldering, chaining and breadboarding. These ultra-bright LEDs have a constant-current driver cooked right into the LED package! The pixels are chainable - so you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
